// Logisim project DDCA EXPO.circ as structural Verilog: 1 circuit, main circuit main
module main (
  input  Hotspot,
  input  Range
);

  wire and_1_out;

  and and_1 (and_1_out, Hotspot, Range);
  LED led_1 (.in(and_1_out));
endmodule
